# Fritzing sketch ESP01-OLED (saved by Fritzing 0.9.3b)
circuit board: 8.46667cm x 5.64444cm

parts:
  ESP01 = ESP8266 ESP01 [part_number=ESP8266 package=THT]
  Power_3_3V = Power plug
  OLED = Grove OLED 128x96 [part_number="OLED 0.96\""]

nets:
  GND: ESP01.GND, Power_3_3V.GND, OLED.GND
  3.3V: ESP01.VCC, ESP01.CH_PD, Power_3_3V.VCC, OLED.VCC
  N1: ESP01.GPIO00, OLED.SCL
  N2: ESP01.GPIO02, OLED.SDA

custom parts:
  ESP8266 ESP01: Generic WiFi Module based on the ESP8266 with onboard PCB antenna and UART communications
